# Fritzing sketch pyowmclock (saved by Fritzing 0.9.3b)
breadboards: 1

parts:
  Part1 = MCP9808 High Accuracy I2C Temperature Sensor [part_number=1782]
  Part2 = Seven-Segment LED Backpack 1.2 Inch Digits [part_number=1270]
  MCU1 = Raspberry Pi Zero

nets:
  N1: Part1.VDD, Part2.VCCIO, MCU1.pin_1, MCU1.pin_17
  GND: Part1.GND, Part2.GND, MCU1.pin_6, MCU1.pin_39
  N2: Part1.SCL, Part2.SCL, MCU1.pin_5
  N3: Part1.SDA, Part2.SDA, MCU1.pin_3
  N4: Part2.VDD, MCU1.pin_2, MCU1.pin_4

custom parts:
  MCP9808 High Accuracy I2C Temperature Sensor: This I2C digital temperature sensor is one of the more accurate/precise we've ever seen, with a typical accuracy of ±0.25°C over the sensor's -40°C to +125°C range and precision of +0.0625°C. They work great with any microcontroller using standard i2c. There are 3 address pins so you can connect up to 8 to a single I2C bus without address collisions. Best of all, a wide voltage range makes is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
  Seven-Segment LED Backpack 1.2 Inch Digits: This jumbo 1.2" 7-segment LED display includes a driver chip for simple control via an I2C interface. The backpack features address-selection jumpers so you can connect up to eight displays on a single I2C bus.
